// Logisim project cpu.circ as structural Verilog: 9 circuits, main circuit Main
module Adder (
  input  [7:0] in_1,
  input  in_2,
  input  [7:0] in_3,
  input  in_4,
  input  in_5,
  output [7:0] out_6
);

  wire [7:0] register_1_q, register_2_q;

  Register register_1 (.D(in_1), .en(in_2), .Q(register_1_q), .clk(in_5), .clr(1'b0));
  Register register_2 (.D(in_3), .en(in_4), .Q(register_2_q), .clk(in_5), .clr(1'b0));
  Adder_part adder_1 (.a(register_1_q), .b(register_2_q), .out(out_6), .cin(1'b0));  // open: cout
endmodule

module CPU_8 (
  input  [7:0] in_1,
  input  [7:0] in_2,
  input  [7:0] in_3,
  input  [7:0] in_4,
  input  [7:0] in_5,
  input  [7:0] in_6,
  input  [7:0] in_7,
  input  [7:0] in_8,
  input  [7:0] in_9,
  input  [7:0] in_10,
  input  [7:0] in_11,
  input  [7:0] in_12,
  input  [7:0] in_13,
  input  [7:0] in_14,
  input  [7:0] in_15,
  input  [7:0] in_16,
  input  [7:0] in_17,
  output [7:0] out_18,
  output [7:0] out_19,
  output [7:0] out_20,
  output [7:0] out_21,
  output [7:0] out_22,
  output [7:0] out_23,
  output [7:0] out_24,
  output [7:0] out_25,
  output [7:0] out_26,
  output [7:0] out_27,
  output [7:0] out_28,
  output [7:0] out_29,
  output [7:0] out_30,
  output [7:0] out_31,
  output [7:0] out_32,
  output [7:0] out_33,
  output out_34,
  output out_35,
  output out_36,
  output out_37,
  output out_38,
  output out_39,
  output out_40,
  output out_41,
  output out_42,
  output out_43,
  output out_44,
  output out_45,
  output out_46,
  output out_47,
  output out_48,
  output out_49,
  output out_50,
  output out_51,
  output out_52,
  output out_53,
  output out_54,
  output out_55,
  output out_56,
  output out_57,
  output out_58,
  output out_59,
  output out_60,
  output out_61,
  output out_62,
  output out_63,
  output out_64,
  output out_65
);

  wire [7:0] multiplexer_1_out;

  Demultiplexer #(.select(4), .disabled(0), .enable("false")) demultiplexer_1 (
    .out0(out_34), .out1(out_36), .out2(out_38), .out3(out_40), .out4(out_42), .out5(out_44), .out6(out_46),
    .out7(out_48), .out8(out_50), .out9(out_52), .out10(out_54), .out11(out_56), .out12(out_58),
    .out13(out_60), .out14(out_62), .out15(out_64), .in(1'b1), .sel(in_17[7:4]));
  Multiplexer #(.select(4), .width(8), .disabled(0), .enable("false")) multiplexer_1 (
    .in0(in_1), .in1(in_2), .in2(in_3), .in3(in_4), .in4(in_5), .in5(in_6), .in6(in_7), .in7(in_8),
    .in8(in_9), .in9(in_10), .in10(in_11), .in11(in_12), .in12(in_13), .in13(in_14), .in14(in_15),
    .in15(in_16), .out(multiplexer_1_out), .sel(in_17[7:4]));
  Demultiplexer #(.select(4), .width(8), .disabled(0), .enable("false")) demultiplexer_2 (
    .out0(out_18), .out1(out_19), .out2(out_20), .out3(out_21), .out4(out_22), .out5(out_23), .out6(out_24),
    .out7(out_25), .out8(out_26), .out9(out_27), .out10(out_28), .out11(out_29), .out12(out_30),
    .out13(out_31), .out14(out_32), .out15(out_33), .in(multiplexer_1_out), .sel(in_17[3:0]));
  Demultiplexer #(.select(4), .disabled(0), .enable("false")) demultiplexer_3 (
    .out0(out_35), .out1(out_37), .out2(out_39), .out3(out_41), .out4(out_43), .out5(out_45), .out6(out_47),
    .out7(out_49), .out8(out_51), .out9(out_53), .out10(out_55), .out11(out_57), .out12(out_59),
    .out13(out_61), .out14(out_63), .out15(out_65), .in(1'b1), .sel(in_17[3:0]));
endmodule

module Memory (
  input  in_1,
  input  [7:0] in_2,
  input  in_3,
  output [7:0] out_4,
  output [7:0] out_5
);

  wire not_1_out;

  not not_1 (not_1_out, in_1);
  Counter counter_1 (.load(in_1), .D(in_2), .count(not_1_out), .Q(out_4), .clk(in_3), .clr(1'b0));  // open: carry
  ROM rom_1 (.addr(out_4), .data(out_5), .sel(1'b1));

  // Notes on the sheet:
  //   contents of rom_1 (hex, n*v repeats v):
  //   61 13 31 31
endmodule

module Main (
);

  wire clock_1_out, cpu_8_1_out_35, cpu_8_1_out_36, cpu_8_1_out_37, cpu_8_1_out_38, cpu_8_1_out_39,
       cpu_8_1_out_41, cpu_8_1_out_43, cpu_8_1_out_45, cpu_8_1_out_47, cpu_8_1_out_49, cpu_8_1_out_51,
       cpu_8_1_out_53, cpu_8_1_out_55, cpu_8_1_out_57;
  wire [7:0] adder_1_out_6, and_1_out_6, cpu_8_1_out_18, cpu_8_1_out_19, cpu_8_1_out_20, cpu_8_1_out_21,
       cpu_8_1_out_22, cpu_8_1_out_23, cpu_8_1_out_24, cpu_8_1_out_25, cpu_8_1_out_26, cpu_8_1_out_27,
       cpu_8_1_out_28, cpu_8_1_out_29, memory_1_out_4, memory_1_out_5, negator_1_out_4, or_1_out_6,
       reg_1_out_4, reg_2_out_4, stack_1_out_5, stack_2_out_5;

  CPU_8 cpu_8_1 (
    .in_1(memory_1_out_4), .in_2(stack_1_out_5), .in_3(stack_2_out_5), .in_4(reg_1_out_4),
    .in_5(reg_2_out_4), .in_6(adder_1_out_6), .in_7(8'h5), .in_8(negator_1_out_4), .in_9(and_1_out_6),
    .in_11(or_1_out_6), .out_18(cpu_8_1_out_18), .out_19(cpu_8_1_out_19), .out_20(cpu_8_1_out_20),
    .out_21(cpu_8_1_out_21), .out_22(cpu_8_1_out_22), .out_23(cpu_8_1_out_23), .out_24(cpu_8_1_out_24),
    .out_25(cpu_8_1_out_25), .out_26(cpu_8_1_out_26), .out_27(cpu_8_1_out_27), .out_28(cpu_8_1_out_28),
    .out_29(cpu_8_1_out_29), .in_17(memory_1_out_5), .out_35(cpu_8_1_out_35), .out_37(cpu_8_1_out_37),
    .out_39(cpu_8_1_out_39), .out_41(cpu_8_1_out_41), .out_43(cpu_8_1_out_43), .out_45(cpu_8_1_out_45),
    .out_47(cpu_8_1_out_47), .out_49(cpu_8_1_out_49), .out_51(cpu_8_1_out_51), .out_53(cpu_8_1_out_53),
    .out_55(cpu_8_1_out_55), .out_57(cpu_8_1_out_57), .out_36(cpu_8_1_out_36), .out_38(cpu_8_1_out_38));  // open: in_10, in_12, in_13, in_14, in_15, in_16, out_30, out_31, out_32, out_33, out_59, out_61, out_63, out_65, out_34, out_40, out_42, out_44, out_46, out_48, out_50, out_52, out_54, out_56, out_58, out_60, out_62, out_64
  Clock clock_1 (.out(clock_1_out));
  Memory memory_1 (
    .in_2(cpu_8_1_out_18), .in_3(clock_1_out), .out_5(memory_1_out_5), .out_4(memory_1_out_4),
    .in_1(cpu_8_1_out_35));
  Stack stack_1 (
    .in_3(cpu_8_1_out_37), .in_4(cpu_8_1_out_36), .in_1(clock_1_out), .in_2(cpu_8_1_out_19),
    .out_5(stack_1_out_5));
  Stack stack_2 (
    .in_3(cpu_8_1_out_39), .in_4(cpu_8_1_out_38), .in_1(clock_1_out), .in_2(cpu_8_1_out_20),
    .out_5(stack_2_out_5));
  Reg reg_1 (.in_1(cpu_8_1_out_21), .out_4(reg_1_out_4), .in_3(clock_1_out), .in_2(cpu_8_1_out_41));
  Reg reg_2 (.in_1(cpu_8_1_out_22), .out_4(reg_2_out_4), .in_3(clock_1_out), .in_2(cpu_8_1_out_43));
  Adder adder_1 (
    .out_6(adder_1_out_6), .in_1(cpu_8_1_out_23), .in_5(clock_1_out), .in_3(cpu_8_1_out_24),
    .in_4(cpu_8_1_out_47), .in_2(cpu_8_1_out_45));
  Negator negator_1 (.in_1(cpu_8_1_out_25), .in_2(cpu_8_1_out_49), .out_4(negator_1_out_4), .in_3(clock_1_out));
  And and_1 (
    .in_1(cpu_8_1_out_26), .in_2(cpu_8_1_out_51), .in_3(cpu_8_1_out_27), .in_4(cpu_8_1_out_53),
    .out_6(and_1_out_6), .in_5(clock_1_out));
  Or or_1 (
    .in_1(cpu_8_1_out_28), .in_2(cpu_8_1_out_55), .in_3(cpu_8_1_out_29), .in_4(cpu_8_1_out_57),
    .out_6(or_1_out_6), .in_5(clock_1_out));
endmodule

module Reg (
  input  [7:0] in_1,
  input  in_2,
  input  in_3,
  output [7:0] out_4
);

  Register register_1 (.D(in_1), .en(in_2), .Q(out_4), .clk(in_3), .clr(1'b0));
endmodule

module Stack (
  input  in_1,
  input  [7:0] in_2,
  input  in_3,
  input  in_4,
  output [7:0] out_5
);

  wire or_1_out;
  wire [7:0] adder_1_out, and_1_out, and_2_out, and_3_out, or_2_out, or_3_out, register_1_q, subtractor_1_out;

  Register register_1 (.D(or_2_out), .en(or_1_out), .Q(register_1_q), .clk(in_1), .clr(1'b0));
  or or_1 (or_1_out, in_4, in_3);
  assign or_2_out = and_2_out | and_1_out;  // OR_Gate or_2, 8 bits wide
  Subtractor subtractor_1 (.a(register_1_q), .b(8'h1), .out(subtractor_1_out), .bin(1'b0));  // open: bout
  assign and_1_out = adder_1_out & {8{in_3}};  // AND_Gate and_1, 8 bits wide
  Adder_part adder_1 (.a(register_1_q), .b(8'h1), .out(adder_1_out), .cin(1'b0));  // open: cout
  assign and_2_out = subtractor_1_out & {8{in_4}};  // AND_Gate and_2, 8 bits wide
  assign and_3_out = register_1_q & {8{in_3}};  // AND_Gate and_3, 8 bits wide
  assign or_3_out = and_2_out | and_3_out;  // OR_Gate or_3, 8 bits wide
  RAM #(.bus("separate")) ram_1 (
    .addr(or_3_out), .din(in_2), .data(out_5), .str(in_3), .sel(1'b1), .clk(in_1), .ld(in_4), .clr(1'b0));
endmodule

module Negator (
  input  [7:0] in_1,
  input  in_2,
  input  in_3,
  output [7:0] out_4
);

  wire [7:0] register_1_q;

  Register register_1 (.D(in_1), .en(in_2), .Q(register_1_q), .clk(in_3), .clr(1'b0));
  Negator_part negator_1 (.in(register_1_q), .out(out_4));
endmodule

module And (
  input  [7:0] in_1,
  input  in_2,
  input  [7:0] in_3,
  input  in_4,
  input  in_5,
  output [7:0] out_6
);

  wire [7:0] register_1_q, register_2_q;

  Register register_1 (.D(in_1), .en(in_2), .Q(register_1_q), .clk(in_5), .clr(1'b0));
  Register register_2 (.D(in_3), .en(in_4), .Q(register_2_q), .clk(in_5), .clr(1'b0));
  assign out_6 = register_1_q & register_2_q;  // AND_Gate and_1, 8 bits wide
endmodule

module Or (
  input  [7:0] in_1,
  input  in_2,
  input  [7:0] in_3,
  input  in_4,
  input  in_5,
  output [7:0] out_6
);

  wire [7:0] register_1_q, register_2_q;

  Register register_1 (.D(in_1), .en(in_2), .Q(register_1_q), .clk(in_5), .clr(1'b0));
  Register register_2 (.D(in_3), .en(in_4), .Q(register_2_q), .clk(in_5), .clr(1'b0));
  assign out_6 = register_1_q | register_2_q;  // OR_Gate or_1, 8 bits wide
endmodule
