// Logisim project cpu.circ as structural Verilog: 5 circuits, main circuit CPU
module Adder (
  input  [7:0] in_1,
  input  in_2,
  input  [7:0] in_3,
  input  in_4,
  input  in_5,
  output [7:0] out_6
);

  wire [7:0] register_1_q, register_2_q;

  Register register_1 (.D(in_1), .en(in_2), .Q(register_1_q), .clk(in_5));  // open: clr
  Register register_2 (.D(in_3), .en(in_4), .Q(register_2_q), .clk(in_5));  // open: clr
  Adder_part adder_1 (.a(register_1_q), .b(register_2_q), .out(out_6), .cin(1'b0));  // open: cout
endmodule

module CPU (
  input  [7:0] in_1,
  input  [7:0] in_2,
  input  [7:0] in_3,
  input  [7:0] in_4,
  input  [7:0] in_5,
  input  [7:0] in_6,
  input  [7:0] in_7,
  input  [7:0] in_8,
  input  [7:0] in_9,
  input  [7:0] in_10,
  input  [7:0] in_11,
  input  [7:0] in_12,
  input  [7:0] in_13,
  input  [7:0] in_14,
  input  [7:0] in_15,
  input  [7:0] in_16,
  input  [7:0] in_17,
  output [7:0] out_18,
  output out_19,
  output [7:0] out_20,
  output out_21,
  output [7:0] out_22,
  output out_23,
  output [7:0] out_24,
  output out_25,
  output [7:0] out_26,
  output out_27,
  output [7:0] out_28,
  output out_29,
  output [7:0] out_30,
  output out_31,
  output [7:0] out_32,
  output out_33,
  output [7:0] out_34,
  output out_35,
  output [7:0] out_36,
  output out_37,
  output [7:0] out_38,
  output out_39,
  output [7:0] out_40,
  output out_41,
  output [7:0] out_42,
  output out_43,
  output [7:0] out_44,
  output out_45,
  output [7:0] out_46,
  output out_47,
  output [7:0] out_48,
  output out_49
);

  wire [7:0] multiplexer_1_out;

  Multiplexer #(.select(4), .width(8), .disabled(0), .enable("false")) multiplexer_1 (
    .in0(in_1), .in1(in_2), .in2(in_3), .in3(in_4), .in4(in_5), .in5(in_6), .in6(in_7), .in7(in_8),
    .in8(in_9), .in9(in_10), .in10(in_11), .in11(in_12), .in12(in_13), .in13(in_14), .in14(in_15),
    .in15(in_16), .out(multiplexer_1_out), .sel(in_17[7:4]));
  Demultiplexer #(.select(4), .width(8), .disabled(0), .enable("false")) demultiplexer_1 (
    .out0(out_18), .out1(out_20), .out2(out_22), .out3(out_24), .out4(out_26), .out5(out_28), .out6(out_30),
    .out7(out_32), .out8(out_34), .out9(out_36), .out10(out_38), .out11(out_40), .out12(out_42),
    .out13(out_44), .out14(out_46), .out15(out_48), .in(multiplexer_1_out), .sel(in_17[3:0]));
  Demultiplexer #(.select(4), .disabled(0), .enable("false")) demultiplexer_2 (
    .out0(out_19), .out1(out_21), .out2(out_23), .out3(out_25), .out4(out_27), .out5(out_29), .out6(out_31),
    .out7(out_33), .out8(out_35), .out9(out_37), .out10(out_39), .out11(out_41), .out12(out_43),
    .out13(out_45), .out14(out_47), .out15(out_49), .in(1'b1), .sel(in_17[3:0]));

  // Notes on the sheet:
  //   out_43: pull=down
  //   out_19: pull=down
  //   out_33: pull=down
  //   out_29: pull=down
  //   out_21: pull=down
  //   out_31: pull=down
  //   out_35: pull=down
  //   out_39: pull=down
  //   out_37: pull=down
  //   out_41: pull=down
  //   out_47: pull=down
  //   out_25: pull=down
  //   out_27: pull=down
  //   out_45: pull=down
  //   out_49: pull=down
  //   out_23: pull=down
endmodule

module Subtractor (
  input  [7:0] in_1,
  input  in_2,
  input  [7:0] in_3,
  input  in_4,
  input  in_5,
  output [7:0] out_6
);

  wire [7:0] register_1_q, register_2_q;

  Register register_1 (.D(in_1), .en(in_2), .Q(register_1_q), .clk(in_5));  // open: clr
  Register register_2 (.D(in_3), .en(in_4), .Q(register_2_q), .clk(in_5));  // open: clr
  Subtractor_part subtractor_1 (.a(register_1_q), .b(register_2_q), .out(out_6), .bin(1'b0));  // open: bout
endmodule

module Memory (
  input  in_1,
  input  [7:0] in_2,
  input  in_3,
  output [7:0] out_4
);

  wire not_1_out;
  wire [7:0] counter_1_q;

  not not_1 (not_1_out, in_1);
  Counter counter_1 (.load(in_1), .D(in_2), .count(not_1_out), .Q(counter_1_q), .clk(in_3), .clr(1'b0));  // open: carry
  RAM #(.bus("separate")) ram_1 (
    .addr(counter_1_q), .din(out_4), .data(out_4), .str(1'b0), .sel(1'b1), .clk(in_3), .ld(1'b1), .clr(1'b0));
endmodule

module Main (
  output [7:0] out_1
);

  wire button_1_out, cpu_1_out_19, cpu_1_out_21, cpu_1_out_23, cpu_1_out_25, cpu_1_out_27;
  wire [7:0] cpu_1_out_18, cpu_1_out_20, cpu_1_out_22, cpu_1_out_24, cpu_1_out_26, memory_1_out_4,
       subtractor_1_out_6;

  Button button_1 (.out(button_1_out));
  Memory memory_1 (.in_2(cpu_1_out_18), .in_3(button_1_out), .out_4(memory_1_out_4), .in_1(cpu_1_out_19));
  CPU cpu_1 (
    .in_1(memory_1_out_4), .in_2(out_1), .in_3(subtractor_1_out_6), .in_4(8'h1), .in_5(8'h2),
    .out_18(cpu_1_out_18), .out_19(cpu_1_out_19), .out_20(cpu_1_out_20), .out_21(cpu_1_out_21),
    .out_22(cpu_1_out_22), .out_23(cpu_1_out_23), .out_24(cpu_1_out_24), .out_25(cpu_1_out_25),
    .out_26(cpu_1_out_26), .out_27(cpu_1_out_27), .in_17(memory_1_out_4));  // open: in_6, in_7, in_8, in_9, in_10, in_11, in_12, in_13, in_14, in_15, in_16, out_28, out_29, out_30, out_31, out_32, out_33, out_34, out_35, out_36, out_37, out_38, out_39, out_40, out_41, out_42, out_43, out_44, out_45, out_46, out_47, out_48, out_49
  Adder adder_1 (
    .out_6(out_1), .in_1(cpu_1_out_20), .in_3(cpu_1_out_22), .in_5(button_1_out), .in_2(cpu_1_out_21),
    .in_4(cpu_1_out_23));
  Subtractor subtractor_1 (
    .in_1(cpu_1_out_24), .in_2(cpu_1_out_25), .in_3(cpu_1_out_26), .in_4(cpu_1_out_27),
    .out_6(subtractor_1_out_6), .in_5(button_1_out));
endmodule
